# Fritzing sketch Palio_v2 (saved by Fritzing 0.9.4)
breadboards: 1

parts:
  ARDUINO = Arduino Mega ADK (Rev3)
  SERVO_-_GAS_PEDAL = Dagu DGServo 9g (Top view) [part_number=RS001B]
  DOWN_CONVT_-_12_to_5_V = LM2596 step down module
  DOWN_CONVT_-_12_to_6_V = LM2596 step down module
  LIN_ACTUATOR_-_CLUTCH = DC Motor
  Relé1 = KY-019 5V Relay Module [package="Breakout board"]
  Relé2 = KY-019 5V Relay Module [package="Breakout board"]
  UP_CONVT_-_12_to_24_V = MT 3608 [part_number=80633 package=dc-dc_converter]
  LIN_ACTUATOR_-_BRAKE = DC Motor
  Relé3 = KY-019 5V Relay Module [package="Breakout board"]
  Relé4 = KY-019 5V Relay Module [package="Breakout board"]
  SWITCH_(ON/OFF) = Square Pushbutton
  CAR_BATTERY_-_12V = LIPO-1000mAh [package=lipo-1000]
  Componente1 = Arduino Uno (Rev3)
  STEP_MOTOR_-_ST_WHEEL1 = Stepper Motor - Bipolar
  STEP_DRIVER1 = Pololu A4988 [package=SO16]
  DOWN_CONVT_-_12_to_8_V1 = LM2596 step down module
  Componente2 = NRF24L01+ Breakout Board
  Componente3 = NRF24L01+ Breakout Board
  SERVO_L = Dagu DGServo 9g (Top view) [part_number=RS001B]
  SERVO_R = Dagu DGServo 9g (Top view) [part_number=RS001B]
  DOWN_CONVT_-_12_to_8_V2 = LM2596 step down module

nets:
  GND: ARDUINO.GND, SERVO_-_GAS_PEDAL.gnd, DOWN_CONVT_-_12_to_5_V.IN-, DOWN_CONVT_-_12_to_5_V.OUT-, DOWN_CONVT_-_12_to_6_V.IN-, DOWN_CONVT_-_12_to_6_V.OUT-, Relé1.-, Relé2.-, UP_CONVT_-_12_to_24_V.IN-, Relé3.-, Relé3.NO, Relé4.-, Relé4.NO, CAR_BATTERY_-_12V.-, STEP_DRIVER1.GND, DOWN_CONVT_-_12_to_8_V1.IN-, DOWN_CONVT_-_12_to_8_V1.OUT-, SERVO_L.gnd, SERVO_R.gnd, DOWN_CONVT_-_12_to_8_V2.IN-, DOWN_CONVT_-_12_to_8_V2.OUT-
  VIN: ARDUINO.VIN, DOWN_CONVT_-_12_to_5_V.OUT+, Relé1.+, Relé2.+, Relé3.+, Relé4.+, Componente1.VIN
  N1: ARDUINO.D2_PWM, SERVO_R.pulse
  N2: ARDUINO.D3_PWM, SERVO_L.pulse
  N3: ARDUINO.D7_PWM, SERVO_-_GAS_PEDAL.pulse
  N4: ARDUINO.D31, Relé1.S
  N5: ARDUINO.D32, Relé2.S
  N6: ARDUINO.D33, Relé3.S
  N7: ARDUINO.D34, Relé4.S
  N8: ARDUINO.D46, Componente3.GND
  N9: ARDUINO.D47, Componente3.VCC
  N10: ARDUINO.D48, Componente3.CE
  N11: ARDUINO.D49, Componente3.CS
  N12: ARDUINO.D50/MISO, Componente3.SCK
  N13: ARDUINO.D51/MOSI, Componente3.MOSI
  N14: ARDUINO.D52/SCK, Componente3.MISO
  N15: ARDUINO.D53/SS, Componente3.IRQ
  N16: SERVO_-_GAS_PEDAL.vcc, DOWN_CONVT_-_12_to_6_V.OUT+
  N17: DOWN_CONVT_-_12_to_5_V.IN+, DOWN_CONVT_-_12_to_6_V.IN+, UP_CONVT_-_12_to_24_V.IN+, Relé3.NC, Relé4.NC, SWITCH_(ON/OFF).leg1, DOWN_CONVT_-_12_to_8_V1.IN+, DOWN_CONVT_-_12_to_8_V2.IN+
  N18: LIN_ACTUATOR_-_CLUTCH.pin_1, Relé1.Common
  N19: LIN_ACTUATOR_-_CLUTCH.pin_2, Relé2.Common
  N20: Relé1.NC, Relé2.NC, UP_CONVT_-_12_to_24_V.OUT+
  N21: Relé1.NO, Relé2.NO, UP_CONVT_-_12_to_24_V.OUT-
  N22: LIN_ACTUATOR_-_BRAKE.pin_1, Relé3.Common
  N23: LIN_ACTUATOR_-_BRAKE.pin_2, Relé4.Common
  N24: SWITCH_(ON/OFF).leg0, CAR_BATTERY_-_12V.+
  N25: Componente1.D9_PWM, Componente2.CE
  N26: Componente1.D10_PWM/SS, Componente2.CS
  N27: Componente1.D11_PWM/MOSI, Componente2.MOSI
  N28: Componente1.D12/MISO, Componente2.MISO
  N29: Componente1.D13/SCK, Componente2.SCK
  N30: Componente1.D3_PWM, STEP_DRIVER1.DIR
  N31: Componente1.D4, STEP_DRIVER1.STEP
  3V3: Componente1.3V3, Componente2.VCC
  GND_2: Componente1.GND, Componente2.GND
  N32: STEP_MOTOR_-_ST_WHEEL1.A, STEP_DRIVER1.2B
  N33: STEP_MOTOR_-_ST_WHEEL1.C, STEP_DRIVER1.1A
  N34: STEP_MOTOR_-_ST_WHEEL1.B, STEP_DRIVER1.1B
  N35: STEP_MOTOR_-_ST_WHEEL1.D, STEP_DRIVER1.2A
  N36: STEP_DRIVER1.VMOT, DOWN_CONVT_-_12_to_8_V1.OUT+
  VCC: SERVO_L.vcc, SERVO_R.vcc, DOWN_CONVT_-_12_to_8_V2.OUT+

custom parts:
  LM2596 step down module: LM2596 DC-DC step down power supply module 3 A.
  KY-019 5V Relay Module: KY-019 5V Relay module, used to control AC circuits.
  MT 3608: DC-DC Step Up Converter
