# Fritzing sketch palio-v3 (saved by Fritzing 0.9.4)
breadboards: 2

parts:
  ARDUINO_MEGA = Arduino Mega ADK (Rev3)
  SERVO_-_GAS_PEDAL = Dagu DGServo 9g (Top view) [part_number=RS001B]
  STEP_MOTOR_-_ST_WHEEL = Stepper Motor - Bipolar
  DOWN_CONVT_-_12_to_5_V = LM2596 step down module
  DOWN_CONVT_-_12_to_6_V = LM2596 step down module
  STEP_DRIVER = Pololu A4988 [package=SO16]
  LIN_ACTUATOR_-_CLUTCH = DC Motor
  Relé1 = KY-019 5V Relay Module [package="Breakout board"]
  Relé2 = KY-019 5V Relay Module [package="Breakout board"]
  UP_CONVT_-_12_to_24_V = MT 3608 [part_number=80633 package=dc-dc_converter]
  LIN_ACTUATOR_-_BRAKE = DC Motor
  Relé_1 = KY-019 5V Relay Module [package="Breakout board"]
  Relé_2 = KY-019 5V Relay Module [package="Breakout board"]
  SWITCH_(ON/OFF) = Square Pushbutton
  CAR_BATTERY_-_12V = LIPO-1000mAh [package=lipo-1000]
  ARDUINO_UNO = Arduino Uno (Rev3)
  SERVO_R_Marcha = Dagu DGServo 9g (Top view) [part_number=RS001B]
  SERVO_L_Marcha = Dagu DGServo 9g (Top view) [part_number=RS001B]
  DOWN_CONVT_-_12_to_8_4_V = LM2596 step down module
  Potenciometro_Freio = SLIDER [package=slider]
  Potenciometro_Embreagem = SLIDER [package=slider]

nets:
  N1: ARDUINO_MEGA.A2, Potenciometro_Freio.S
  N2: ARDUINO_MEGA.A3, Potenciometro_Embreagem.S
  N3: ARDUINO_MEGA.D10_PWM, SERVO_R_Marcha.pulse
  N4: ARDUINO_MEGA.D9_PWM, SERVO_L_Marcha.pulse
  GND: ARDUINO_MEGA.GND, SERVO_-_GAS_PEDAL.gnd, DOWN_CONVT_-_12_to_5_V.IN-, DOWN_CONVT_-_12_to_5_V.OUT-, DOWN_CONVT_-_12_to_6_V.IN-, DOWN_CONVT_-_12_to_6_V.OUT-, STEP_DRIVER.GND, Relé1.-, Relé2.-, UP_CONVT_-_12_to_24_V.IN-, Relé_1.-, Relé_1.NC, Relé_2.-, Relé_2.NC, CAR_BATTERY_-_12V.-, ARDUINO_UNO.GND, SERVO_R_Marcha.gnd, SERVO_L_Marcha.gnd, DOWN_CONVT_-_12_to_8_4_V.IN-, DOWN_CONVT_-_12_to_8_4_V.OUT-, Potenciometro_Freio.A, Potenciometro_Embreagem.A
  VIN: ARDUINO_MEGA.VIN, DOWN_CONVT_-_12_to_5_V.OUT+, STEP_DRIVER.VDD, Relé1.+, Relé2.+, Relé_1.+, Relé_2.+, ARDUINO_UNO.VIN, Potenciometro_Freio.E, Potenciometro_Embreagem.E
  N5: ARDUINO_MEGA.D7_PWM, SERVO_-_GAS_PEDAL.pulse
  N6: ARDUINO_MEGA.D31, Relé1.S
  N7: ARDUINO_MEGA.D32, Relé2.S
  N8: ARDUINO_MEGA.D33, Relé_1.S
  N9: ARDUINO_MEGA.D34, Relé_2.S
  N10: SERVO_-_GAS_PEDAL.vcc, DOWN_CONVT_-_12_to_6_V.OUT+
  N11: STEP_MOTOR_-_ST_WHEEL.A, STEP_DRIVER.2B
  N12: STEP_MOTOR_-_ST_WHEEL.C, STEP_DRIVER.1A
  N13: STEP_MOTOR_-_ST_WHEEL.B, STEP_DRIVER.1B
  N14: STEP_MOTOR_-_ST_WHEEL.D, STEP_DRIVER.2A
  N15: DOWN_CONVT_-_12_to_5_V.IN+, DOWN_CONVT_-_12_to_6_V.IN+, STEP_DRIVER.VMOT, UP_CONVT_-_12_to_24_V.IN+, Relé_1.NO, Relé_2.NO, SWITCH_(ON/OFF).leg1, DOWN_CONVT_-_12_to_8_4_V.IN+
  N16: STEP_DRIVER.STEP, ARDUINO_UNO.D8
  N17: STEP_DRIVER.DIR, ARDUINO_UNO.D10_PWM/SS
  N18: LIN_ACTUATOR_-_CLUTCH.pin_1, Relé1.Common
  N19: LIN_ACTUATOR_-_CLUTCH.pin_2, Relé2.Common
  N20: Relé1.NC, Relé2.NC, UP_CONVT_-_12_to_24_V.OUT-
  N21: Relé1.NO, Relé2.NO, UP_CONVT_-_12_to_24_V.OUT+
  N22: LIN_ACTUATOR_-_BRAKE.pin_1, Relé_1.Common
  N23: LIN_ACTUATOR_-_BRAKE.pin_2, Relé_2.Common
  N24: SWITCH_(ON/OFF).leg0, CAR_BATTERY_-_12V.+
  VCC: SERVO_R_Marcha.vcc, SERVO_L_Marcha.vcc, DOWN_CONVT_-_12_to_8_4_V.OUT+

custom parts:
  LM2596 step down module: LM2596 DC-DC step down power supply module 3 A.
  KY-019 5V Relay Module: KY-019 5V Relay module, used to control AC circuits.
  MT 3608: DC-DC Step Up Converter
