# Fritzing sketch palio-v5 (saved by Fritzing 0.9.4)
breadboards: 2

parts:
  ARDUINO_MEGA = Arduino Mega ADK (Rev3)
  SERVO_-_GAS_PEDAL = Dagu DGServo 9g (Top view) [part_number=RS001B]
  STEP_MOTOR_-_ST_WHEEL = Stepper Motor - Bipolar
  DOWN_CONVT_-_12_to_5_V = LM2596 step down module
  DOWN_CONVT_-_12_to_6_V = LM2596 step down module
  STEP_DRIVER = Pololu A4988 [package=SO16]
  LIN_ACTUATOR_-_CLUTCH = DC Motor
  Relé1 = KY-019 5V Relay Module [package="Breakout board"]
  Relé2 = KY-019 5V Relay Module [package="Breakout board"]
  UP_CONVT_-_12_to_24_V = MT 3608 [part_number=80633 package=dc-dc_converter]
  LIN_ACTUATOR_-_BRAKE = DC Motor
  Relé_1 = KY-019 5V Relay Module [package="Breakout board"]
  Relé_2 = KY-019 5V Relay Module [package="Breakout board"]
  SWITCH_(ON/OFF) = Square Pushbutton
  CAR_BATTERY_-_12V = LIPO-1000mAh [package=lipo-1000]
  ARDUINO_UNO = Arduino Uno (Rev3)
  SERVO_R_Marcha = Dagu DGServo 9g (Top view) [part_number=RS001B]
  SERVO_L_Marcha = Dagu DGServo 9g (Top view) [part_number=RS001B]
  DOWN_CONVT_-_12_to_8_4_V = LM2596 step down module
  Potenciometro_Freio = SLIDER [package=slider]
  Potenciometro_Embreagem = SLIDER [package=slider]
  Componente1 = NRF24L01+ Breakout Board
  Componente2 = NRF24L01+ Breakout Board  # not connected
  Componente3 = NRF24L01+ Breakout Board

nets:
  N1: ARDUINO_MEGA.A2, Potenciometro_Freio.S
  N2: ARDUINO_MEGA.A3, Potenciometro_Embreagem.S
  N3: ARDUINO_MEGA.D10_PWM, SERVO_R_Marcha.pulse
  N4: ARDUINO_MEGA.D9_PWM, SERVO_L_Marcha.pulse
  GND: ARDUINO_MEGA.GND, SERVO_-_GAS_PEDAL.gnd, DOWN_CONVT_-_12_to_5_V.IN-, DOWN_CONVT_-_12_to_5_V.OUT-, DOWN_CONVT_-_12_to_6_V.IN-, DOWN_CONVT_-_12_to_6_V.OUT-, STEP_DRIVER.GND, Relé1.-, Relé2.-, UP_CONVT_-_12_to_24_V.IN-, Relé_1.-, Relé_1.NC, Relé_2.-, Relé_2.NC, CAR_BATTERY_-_12V.-, ARDUINO_UNO.GND, SERVO_R_Marcha.gnd, SERVO_L_Marcha.gnd, DOWN_CONVT_-_12_to_8_4_V.IN-, DOWN_CONVT_-_12_to_8_4_V.OUT-, Potenciometro_Freio.A, Potenciometro_Embreagem.A, Componente1.MISO, Componente1.IRQ, Componente3.GND
  VIN: ARDUINO_MEGA.VIN, DOWN_CONVT_-_12_to_5_V.OUT+, STEP_DRIVER.VDD, Relé1.+, Relé2.+, Relé_1.+, Relé_2.+, ARDUINO_UNO.VIN, Potenciometro_Freio.E, Potenciometro_Embreagem.E
  N5: ARDUINO_MEGA.D7_PWM, SERVO_-_GAS_PEDAL.pulse
  N6: ARDUINO_MEGA.D31, Relé1.S
  N7: ARDUINO_MEGA.D32, Relé2.S
  N8: ARDUINO_MEGA.D33, Relé_1.S
  N9: ARDUINO_MEGA.D34, Relé_2.S
  N10: ARDUINO_MEGA.D48, Componente1.GND
  N11: ARDUINO_MEGA.D49, Componente1.VCC
  N12: ARDUINO_MEGA.D50/MISO, Componente1.CE
  N13: ARDUINO_MEGA.D51/MOSI, Componente1.CS
  N14: ARDUINO_MEGA.D52/SCK, Componente1.SCK
  N15: ARDUINO_MEGA.D53/SS, Componente1.MOSI
  N16: SERVO_-_GAS_PEDAL.vcc, DOWN_CONVT_-_12_to_6_V.OUT+
  N17: STEP_MOTOR_-_ST_WHEEL.A, STEP_DRIVER.2B
  N18: STEP_MOTOR_-_ST_WHEEL.C, STEP_DRIVER.1A
  N19: STEP_MOTOR_-_ST_WHEEL.B, STEP_DRIVER.1B
  N20: STEP_MOTOR_-_ST_WHEEL.D, STEP_DRIVER.2A
  N21: DOWN_CONVT_-_12_to_5_V.IN+, DOWN_CONVT_-_12_to_6_V.IN+, STEP_DRIVER.VMOT, UP_CONVT_-_12_to_24_V.IN+, Relé_1.NO, Relé_2.NO, SWITCH_(ON/OFF).leg1, DOWN_CONVT_-_12_to_8_4_V.IN+
  N22: STEP_DRIVER.STEP, ARDUINO_UNO.D8
  N23: STEP_DRIVER.DIR, ARDUINO_UNO.D10_PWM/SS
  N24: LIN_ACTUATOR_-_CLUTCH.pin_1, Relé1.Common
  N25: LIN_ACTUATOR_-_CLUTCH.pin_2, Relé2.Common
  N26: Relé1.NC, Relé2.NC, UP_CONVT_-_12_to_24_V.OUT-
  N27: Relé1.NO, Relé2.NO, UP_CONVT_-_12_to_24_V.OUT+
  N28: LIN_ACTUATOR_-_BRAKE.pin_1, Relé_1.Common
  N29: LIN_ACTUATOR_-_BRAKE.pin_2, Relé_2.Common
  N30: SWITCH_(ON/OFF).leg0, CAR_BATTERY_-_12V.+
  N31: ARDUINO_UNO.D11_PWM/MOSI, Componente3.MOSI
  N32: ARDUINO_UNO.D12/MISO, Componente3.MISO
  N33: ARDUINO_UNO.D13/SCK, Componente3.SCK
  N34: ARDUINO_UNO.D3_PWM, Componente3.CE
  N35: ARDUINO_UNO.D4, Componente3.CS
  3V3: ARDUINO_UNO.3V3, Componente3.VCC
  VCC: SERVO_R_Marcha.vcc, SERVO_L_Marcha.vcc, DOWN_CONVT_-_12_to_8_4_V.OUT+

custom parts:
  LM2596 step down module: LM2596 DC-DC step down power supply module 3 A.
  KY-019 5V Relay Module: KY-019 5V Relay module, used to control AC circuits.
  MT 3608: DC-DC Step Up Converter
