# Fritzing sketch palio_v1 (saved by Fritzing 0.9.4)
breadboards: 1

parts:
  ARDUINO = Arduino Mega ADK (Rev3)
  SERVO_-_GAS_PEDAL = Dagu DGServo 9g (Top view) [part_number=RS001B]
  STEP_MOTOR_-_ST_WHEEL = Stepper Motor - Bipolar
  DOWN_CONVT_-_12_to_5_V = LM2596 step down module
  DOWN_CONVT_-_12_to_6_V = LM2596 step down module
  STEP_DRIVER = Pololu A4988 [package=SO16]
  DOWN_CONVT_-_12_to_8_V = LM2596 step down module
  LIN_ACTUATOR_-_CLUTCH = DC Motor
  Relé1 = KY-019 5V Relay Module [package="Breakout board"]
  Relé2 = KY-019 5V Relay Module [package="Breakout board"]
  UP_CONVT_-_12_to_24_V = MT 3608 [part_number=80633 package=dc-dc_converter]
  LIN_ACTUATOR_-_BRAKE = DC Motor
  Relé3 = KY-019 5V Relay Module [package="Breakout board"]
  Relé4 = KY-019 5V Relay Module [package="Breakout board"]
  SWITCH_(ON/OFF) = Square Pushbutton
  CAR_BATTERY_-_12V = LIPO-1000mAh [package=lipo-1000]

nets:
  GND: ARDUINO.GND, SERVO_-_GAS_PEDAL.gnd, DOWN_CONVT_-_12_to_5_V.IN-, DOWN_CONVT_-_12_to_5_V.OUT-, DOWN_CONVT_-_12_to_6_V.IN-, DOWN_CONVT_-_12_to_6_V.OUT-, STEP_DRIVER.GND, DOWN_CONVT_-_12_to_8_V.IN-, DOWN_CONVT_-_12_to_8_V.OUT-, Relé1.-, Relé2.-, UP_CONVT_-_12_to_24_V.IN-, Relé3.-, Relé3.NO, Relé4.-, Relé4.NO, CAR_BATTERY_-_12V.-
  N1: ARDUINO.D10_PWM, STEP_DRIVER.DIR
  N2: ARDUINO.D8_PWM, STEP_DRIVER.STEP
  VIN: ARDUINO.VIN, DOWN_CONVT_-_12_to_5_V.OUT+, STEP_DRIVER.VDD, Relé1.+, Relé2.+, Relé3.+, Relé4.+
  N3: ARDUINO.D7_PWM, SERVO_-_GAS_PEDAL.pulse
  N4: ARDUINO.D31, Relé1.S
  N5: ARDUINO.D32, Relé2.S
  N6: ARDUINO.D33, Relé3.S
  N7: ARDUINO.D34, Relé4.S
  N8: SERVO_-_GAS_PEDAL.vcc, DOWN_CONVT_-_12_to_6_V.OUT+
  N9: STEP_MOTOR_-_ST_WHEEL.A, STEP_DRIVER.2B
  N10: STEP_MOTOR_-_ST_WHEEL.C, STEP_DRIVER.1A
  N11: STEP_MOTOR_-_ST_WHEEL.B, STEP_DRIVER.1B
  N12: STEP_MOTOR_-_ST_WHEEL.D, STEP_DRIVER.2A
  N13: DOWN_CONVT_-_12_to_5_V.IN+, DOWN_CONVT_-_12_to_6_V.IN+, DOWN_CONVT_-_12_to_8_V.IN+, UP_CONVT_-_12_to_24_V.IN+, Relé3.NC, Relé4.NC, SWITCH_(ON/OFF).leg1
  N14: STEP_DRIVER.VMOT, DOWN_CONVT_-_12_to_8_V.OUT+
  N15: LIN_ACTUATOR_-_CLUTCH.pin_1, Relé1.Common
  N16: LIN_ACTUATOR_-_CLUTCH.pin_2, Relé2.Common
  N17: Relé1.NC, Relé2.NC, UP_CONVT_-_12_to_24_V.OUT+
  N18: Relé1.NO, Relé2.NO, UP_CONVT_-_12_to_24_V.OUT-
  N19: LIN_ACTUATOR_-_BRAKE.pin_1, Relé3.Common
  N20: LIN_ACTUATOR_-_BRAKE.pin_2, Relé4.Common
  N21: SWITCH_(ON/OFF).leg0, CAR_BATTERY_-_12V.+

custom parts:
  LM2596 step down module: LM2596 DC-DC step down power supply module 3 A.
  KY-019 5V Relay Module: KY-019 5V Relay module, used to control AC circuits.
  MT 3608: DC-DC Step Up Converter
